# Fritzing sketch Theremin (saved by Fritzing 0.9.3b)
circuit board: 8.46667cm x 5.64444cm
breadboards: 1

parts:
  Raspberry_Pi1 = Raspberry Pi B+
  hc-sr1 = hc-sr04 [part_number=Frequenzsensor]
  hc-sr2 = hc-sr04 [part_number=Volumesensor]
  R1 = Resistor [tolerance=±5% resistance=1k package=THT]
  R2 = Resistor [tolerance=±5% resistance=2.2k package=THT]
  R3 = Resistor [tolerance=±5% resistance=1k package=THT]
  R4 = Resistor [tolerance=±5% resistance=2.2k package=THT]
  Grove1 = Grove OLED 128x96 [part_number="Display Tonanzeige"]
  NEOPIXEL1 = Neopixel Strip -- White (60/m) [part_number="LED Antenne"]
  NEOPIXEL2 = Neopixel Strip -- White (60/m) [part_number="LED Gehäuse"]
  Netzteil = Screw terminal - 2 pins [package=THT]

nets:
  3V3: Raspberry_Pi1.3v3, Grove1.VCC
  N1: Raspberry_Pi1.GPIO2, Grove1.SDA
  N2: Raspberry_Pi1.GPIO3, Grove1.SCL
  GND: Raspberry_Pi1.GND, hc-sr1.GND, hc-sr2.GND, R2.Pin_1, R4.Pin_1, Grove1.GND, NEOPIXEL1.GND, NEOPIXEL2.GND, Netzteil.pin2
  N3: Raspberry_Pi1.GPIO17, hc-sr1.Trig
  N4: Raspberry_Pi1.GPIO27, R1.Pin_1, R2.Pin_0
  N5: Raspberry_Pi1.GPIO5, hc-sr2.Trig
  N6: Raspberry_Pi1.GPIO6, R3.Pin_1, R4.Pin_0
  N7: Raspberry_Pi1.GPIO21, NEOPIXEL1.DI
  N8: Raspberry_Pi1.GPIO18, NEOPIXEL2.DI
  VCC: Raspberry_Pi1.5V, hc-sr1.VCC, hc-sr2.VCC
  N9: hc-sr1.Echo, R1.Pin_0
  N10: hc-sr2.Echo, R3.Pin_0
  +5V: NEOPIXEL1.+5V, NEOPIXEL2.+5V, Netzteil.pin1

custom parts:
  Neopixel Strip -- White (60/m): Neopixel Strip, White, 60 pixels per meter.
